# Fritzing sketch PhineBox schematics (saved by Fritzing 0.9.3b)
breadboards: 1

parts:
  Mikrocontroller = Arduino Nano (Rev3.0)
  DFRobot_DFPlayer_Mini1 = DFRobot DFPlayer Mini [part_number=DFR0299]
  Kartenleser = RFID-RC522-v2
  Laderegler = mystery part, 7 pins [chip_label="DDO6CVSA battery controller" part_number=FM3209F]
  Audioverstärker = mystery part, 9 pins [chip_label="2x 3W D-class AMP" part_number=PAM8403]
  SPKR1 = Loudspeaker
  SPKR2 = Loudspeaker
  Power_plug1 = Power plug
  18650_-_4_2V = Battery
  blau = Pushbutton [package="[THT]"]
  schwarz = Pushbutton [package="[THT]"]
  weiß = Pushbutton [package="[THT]"]
  grün = Pushbutton [package="[THT]"]
  rot = Pushbutton [package="[THT]"]
  gelb = Pushbutton [package="[THT]"]
  Starterbutton = Pushbutton [package="[THT]"]
  2-Relais-Shield = mystery part, 4 pins [chip_label="Relais Shield"]
  TRS1 = Audio Jack (TRS) 3.5mm [package="4Ucon 08780 [THT]"]
  NO-pin6_(System) = Screw terminal - 2 pins [package=THT]
  NC-pin5_(Lautsprecher) = Screw terminal - 2 pins [package=THT]
  R1 = 1kΩ Resistor [part_number=1000kOhm package=THT]
  R2 = Resistor [tolerance=±5% resistance=330 package=THT]
  LED1 = LED - 5mm [color="Blue (470nm)" package="5 mm [THT]"]

nets:
  N1: Mikrocontroller.GND, Kartenleser.RST, Laderegler.pin1, Laderegler.pin3, Audioverstärker.pin2, 2-Relais-Shield.pin4, LED1.cathode
  N2: Mikrocontroller.D2, DFRobot_DFPlayer_Mini1.TX
  N3: Mikrocontroller.D3, R1.Pin_0
  N4: Mikrocontroller.D4, DFRobot_DFPlayer_Mini1.BUSY
  N5: Mikrocontroller.D5, 2-Relais-Shield.pin2
  N6: Mikrocontroller.D6, 2-Relais-Shield.pin1
  N7: Mikrocontroller.D7, R2.Pin_0
  N8: Mikrocontroller.D9, Kartenleser.IRQ
  N9: Mikrocontroller.D10, Kartenleser.SCK
  N10: Mikrocontroller.D11/MOSI, Kartenleser.MOSI
  N11: Mikrocontroller.D12/MISO, Kartenleser.MISO
  VIN: Mikrocontroller.VIN, DFRobot_DFPlayer_Mini1.VCC
  N12: Mikrocontroller.A5, gelb.Pin_1, gelb.Pin_2
  N13: Mikrocontroller.A4, rot.Pin_1, rot.Pin_2
  N14: Mikrocontroller.A3, grün.Pin_1, grün.Pin_2
  N15: Mikrocontroller.A2, weiß.Pin_2
  N16: Mikrocontroller.A1, schwarz.Pin_2
  N17: Mikrocontroller.A0, blau.Pin_2
  N18: Mikrocontroller.3V3, Kartenleser.3_3V
  N19: Mikrocontroller.D13/SCK, Kartenleser.SDA
  N20: DFRobot_DFPlayer_Mini1.RX, R1.Pin_1
  N21: DFRobot_DFPlayer_Mini1.DAC_R, Audioverstärker.pin5, TRS1.Ring
  N22: DFRobot_DFPlayer_Mini1.DAC_L, Audioverstärker.pin3, TRS1.Tip
  N23: DFRobot_DFPlayer_Mini1.GND-1, DFRobot_DFPlayer_Mini1.GND-2, Audioverstärker.pin4, TRS1.Sleeve
  N24: Laderegler.pin2, Starterbutton.Pin_3, NO-pin6_(System).pin2
  N25: Laderegler.pin4, 18650_-_4_2V.-
  N26: Laderegler.pin5, 18650_-_4_2V.+
  N27: Laderegler.pin6, Power_plug1.GND
  N28: Laderegler.pin7, Power_plug1.VCC
  N29: Audioverstärker.pin1, NC-pin5_(Lautsprecher).pin1
  N30: Audioverstärker.pin6, SPKR1.pin1
  N31: Audioverstärker.pin7, SPKR1.pin2
  N32: Audioverstärker.pin8, SPKR2.pin1
  N33: Audioverstärker.pin9, SPKR2.pin2
  N34: blau.Pin_4, schwarz.Pin_3, schwarz.Pin_4, weiß.Pin_3, weiß.Pin_4, grün.Pin_3, grün.Pin_4, rot.Pin_3, rot.Pin_4, gelb.Pin_3, gelb.Pin_4
  N35: Starterbutton.Pin_1, Starterbutton.Pin_2, 2-Relais-Shield.pin3, NO-pin6_(System).pin1, NC-pin5_(Lautsprecher).pin2
  N36: R2.Pin_1, LED1.anode

notes:
  3adrig, Daten
  3adrig, 2x 5V + GND
  7adrig, diverse
  UNTER RECHTER ABDECKUNG
  UNTER LINKER ABDECKUNG
  IM DECKEL

custom parts:
  RFID-RC522-v2: A simple China made RFID-RC522 Reader; do check the pin labels, as this is a MFRC522 based clone.
  1kΩ Resistor: A generic resistor (0.25W)
